# Fritzing sketch Automatic_Parking_System (saved by Fritzing 1.0.5)
breadboards: 2

parts:
  ESP8266 = Amica NodeMCU DEVKIT 1.0
  M1 = fc-51 [package=THT]
  M2 = fc-51 [package=THT]
  M3 = fc-51 [package=THT]
  M4 = fc-51 [package=THT]
  M5 = fc-51 [package=THT]
  M6 = fc-51 [package=THT]
  J1 = Basic Servo
  M8 = pcf8574 io expansion board [package=THT]
  VCC1 = Battery [internal_resistance=0.1Ω]
  RFID_IC_RC522 = RFID-RC522-v2

nets:
  VCC: ESP8266.pin1, ESP8266.pin_10, ESP8266.pin_26, M8.VCC, RFID_IC_RC522.3.3V
  GND: ESP8266.pin2, ESP8266.pin_9, ESP8266.pin_25, ESP8266.pin_29, M1.pin2, M2.pin2, M3.pin2, M4.pin2, M5.pin2, M6.pin2, J1.gnd, M8.GND, VCC1.-
  N1: ESP8266.pin5, RFID_IC_RC522.SDA
  N2: ESP8266.pin6, RFID_IC_RC522.MOSI
  N3: ESP8266.pin7, RFID_IC_RC522.MISO
  N4: ESP8266.pin8, RFID_IC_RC522.SCK
  N5: ESP8266.pin_11, J1.pulse
  N6: ESP8266.pin_13, M8.SDA
  N7: ESP8266.pin_14, M8.SCL
  N8: ESP8266.pin_15, M6.pin1
  N9: M1.pin1, M8.O4
  N10: M1.pin3, M2.pin3, M3.pin3, M4.pin3, M5.pin3, VCC1.+
  N11: M2.pin1, M8.O3
  N12: M3.pin1, M8.O2
  N13: M4.pin1, M8.O1
  N14: M5.pin1, M8.O0
  N15: M6.pin3, J1.vcc

custom parts:
  pcf8574 io expansion board: pcf8574 io expansion board.
  RFID-RC522-v2: A simple China made RFID-RC522 Reader; do check the pin labels, as this is a MFRC522 based clone.
